// Logisim project alu.circ as structural Verilog: 1 circuit, main circuit alu
module alu (
  input  [31:0] A,
  input  [31:0] B,
  input  [3:0] ALUSel,
  output [31:0] Result
);

  wire AL0, allzero, and_2_out, BL0, comparator_4_lt, comparator_5_eq, comparator_6_eq, situation;
  wire [4:0] bitfinder_1_index, bitfinder_2_index;
  wire [6:0] bitadder_1_out;
  wire [31:0] AA, add, and1, BB, bit_extender_3_out, cnto, divu, high, mulh, mulh1, mulh2, mulhu, mult,
       multiplexer_1_out, multiplier_1_out, negator_1_out, negator_2_out, negator_3_out, negator_4_out, or1,
       remu, sll1, slt, sra1, srl1, sub, subtractor_1_out, xor1;

  Adder #(.width(1)) adder_1 (.a(AL0), .b(BL0), .out(situation));  // open: cin, cout
  Comparator #(.width(32)) comparator_1 (.a({32{1'b0}}), .b(A), .gt(AL0));  // open: eq, lt
  Comparator #(.width(32)) comparator_2 (.a(B), .b({32{1'b0}}), .lt(BL0));  // open: gt, eq
  Comparator #(.width(32)) comparator_3 (.a(high), .b({32{1'b0}}), .eq(allzero));  // open: gt, lt
  Multiplier #(.width(32)) multiplier_1 (.a(AA), .b(BB), .out(multiplier_1_out), .cout(high));  // open: cin
  Negator #(.width(32)) negator_1 (.in(high), .out(negator_1_out));
  Subtractor #(.width(32)) subtractor_1 (.a(negator_1_out), .b(32'h1), .out(subtractor_1_out));  // open: bin, bout
  Multiplexer #(.width(32), .enable("false")) multiplexer_1 (
    .in0(subtractor_1_out), .in1(high), .out(multiplexer_1_out), .sel(allzero));
  assign xor1 = A ^ B;  // XOR_Gate xor_1, 32 bits wide
  assign or1 = A | B;  // OR_Gate or_1, 32 bits wide
  assign and1 = A & B;  // AND_Gate and_1, 32 bits wide
  Adder #(.width(32)) adder_2 (.a(A), .b(B), .out(add));  // open: cin, cout
  Shifter #(.width(32), .shift("lr")) shifter_1 (.in(A), .\dist (B[4:0]), .out(srl1));
  Shifter #(.width(32), .shift("ar")) shifter_2 (.in(A), .\dist (B[4:0]), .out(sra1));
  Shifter #(.width(32)) shifter_3 (.in(A), .\dist (B[4:0]), .out(sll1));
  Comparator #(.width(32)) comparator_4 (.a(A), .b(B), .lt(comparator_4_lt));  // open: gt, eq
  Divider #(.width(32)) divider_1 (.a(A), .b(B), .out(divu));  // open: upper, rem
  Divider #(.width(32)) divider_2 (.a(A), .b(B), .rem(remu));  // open: out, upper
  Multiplier #(.width(32)) multiplier_2 (.a(A), .b(B), .out(mult));  // open: cin, cout
  Multiplier #(.width(32)) multiplier_3 (.a(A), .b(B), .cout(mulhu));  // open: out, cin
  Subtractor #(.width(32)) subtractor_2 (.a(A), .b(B), .out(sub));  // open: bin, bout
  BitAdder #(.width(32)) bitadder_1 (.in0(A), .in1(B), .out(bitadder_1_out));
  Negator #(.width(32)) negator_2 (.in(A), .out(negator_2_out));
  Negator #(.width(32)) negator_3 (.in(B), .out(negator_3_out));
  BitFinder #(.width(32), .\type ("high0")) bitfinder_1 (
    .in(multiplier_1_out), .index(bitfinder_1_index));  // open: found
  Negator #(.width(32)) negator_4 (.in(multiplier_1_out), .out(negator_4_out));
  assign slt = {{31{1'b0}}, comparator_4_lt};  // Bit_Extender bit_extender_1
  assign cnto = {{25{1'b0}}, bitadder_1_out};  // Bit_Extender bit_extender_2
  Multiplexer #(.width(32), .enable("false")) multiplexer_2 (.in0(A), .in1(negator_2_out), .out(AA), .sel(AL0));
  Multiplexer #(.width(32), .enable("false")) multiplexer_3 (.in0(B), .in1(negator_3_out), .out(BB), .sel(BL0));
  Multiplier #(.width(32)) multiplier_4 (.a(AA), .b(BB), .cout(mulh1));  // open: out, cin
  Comparator #(.width(5), .mode("unsigned")) comparator_5 (
    .a({5{1'b1}}), .b(bitfinder_1_index), .eq(comparator_5_eq));  // open: gt, lt
  BitFinder #(.width(32), .\type ("high0")) bitfinder_2 (.in(negator_4_out), .index(bitfinder_2_index));  // open: found
  Adder #(.width(32)) adder_3 (.a(bit_extender_3_out), .b(multiplexer_1_out), .out(mulh2));  // open: cin, cout
  Comparator #(.width(5), .mode("unsigned")) comparator_6 (
    .a({5{1'b1}}), .b(bitfinder_2_index), .eq(comparator_6_eq));  // open: gt, lt
  assign bit_extender_3_out = {{31{1'b0}}, and_2_out};  // Bit_Extender bit_extender_3
  Multiplexer #(.select(4), .width(32), .enable("false")) multiplexer_4 (
    .in0(add), .in1(and1), .in2(or1), .in3(xor1), .in4(srl1), .in5(sra1), .in6(sll1), .in7(slt), .in8(divu),
    .in9(remu), .in10(mult), .in11(mulhu), .in12(sub), .in13(cnto), .in14(mulh), .out(Result), .sel(ALUSel));  // open: in15
  Multiplexer #(.width(32), .enable("false")) multiplexer_5 (.in0(mulh1), .in1(mulh2), .out(mulh), .sel(situation));
  and and_2 (and_2_out, comparator_5_eq, comparator_6_eq);

  // Notes on the sheet:
  //   INPUTS to your circuit
  //   DON'T CHANGE THE LOCATIONS OF THE INPUTS AND OUTPUTS!
  //   OUTPUT from your circuit
endmodule
