// Logisim project cpu.circ as structural Verilog: 1 circuit, main circuit main
module main (
  input  [31:0] INSTRUCTION,
  input  CLOCK,
  output [31:0] FETCH_ADDRESS,
  output [31:0] ra,
  output [31:0] sp,
  output [31:0] t0,
  output [31:0] t1,
  output [31:0] t2,
  output [31:0] s0,
  output [31:0] s1,
  output [31:0] a0
);

  wire aa, Asel, BrUn, Bsel, comparator_4_eq, comparator_5_eq, comparator_6_eq, comparator_7_eq,
       comparator_8_eq, comparator_9_eq, comparator_10_eq, comparator_11_eq, comparator_12_eq,
       comparator_13_eq, comparator_14_eq, comparator_15_eq, comparator_22_eq, comparator_23_eq,
       comparator_24_eq, comparator_25_eq, comparator_27_eq, comparator_28_eq, comparator_29_eq,
       comparator_30_eq, comparator_31_eq, comparator_32_eq, comparator_33_eq, comparator_34_eq,
       comparator_35_eq, comparator_36_eq, comparator_37_eq, comparator_38_eq, comparator_39_eq,
       comparator_40_eq, comparator_41_eq, comparator_42_eq, comparator_43_eq, comparator_44_eq,
       comparator_45_eq, DMEM_p9, DMEM_p10, I1, I2, I3, J, MenRW, not_1_out, PCSel, R, regWen, S, SB,
       SignedBrLT, U, UnsignedBrLT;
  wire [1:0] WBSel;
  wire [2:0] func3, ImmSel;
  wire [3:0] ALUsel, bit_extender_6_out;
  wire [4:0] controlled_buffer_4_out, controlled_buffer_7_out, controlled_buffer_14_out,
       controlled_buffer_20_out, controlled_buffer_25_out, controlled_buffer_33_out,
       controlled_buffer_36_out, controlled_buffer_38_out, controlled_buffer_40_out, instr;
  wire [6:0] func7, INSTRUCTION_t;
  wire [15:0] bit_extender_7_out;
  wire [31:0] A, B, bit_extender_5_out, bit_extender_8_out, fetch_addr4, Imm, ImmI, ins, multiplexer_5_out,
       multiplexer_14_out, multiplexer_15_out, multiplexer_16_out, multiplexer_17_out, ReadData, ReadData2,
       register_1_q, result, Rrs1, Rrs2, shifter_1_out, shifter_2_out, shifter_3_out, shifter_4_out,
       shifter_5_out, subtractor_1_out, subtractor_2_out, subtractor_3_out, WB;
  wire [31:1] ImmB;
  wire [31:11] ImmS;
  wire [31:15] ImmJ;

  Register #(.width(32)) register_1 (.D(INSTRUCTION), .clk(CLOCK), .Q(register_1_q));  // open: en, clr
  Shifter #(.width(32), .shift("ar")) shifter_1 (
    .in({ImmB[31:11], func7[5:0], ImmB[4:1], 1'b0}), .\dist (5'b00010), .out(shifter_1_out));
  Multiplexer #(.width(32), .enable("false")) multiplexer_1 (
    .in0(register_1_q), .in1(ins),
    .out({func7, ImmI[4:0], ImmJ[19:15], func3, ImmB[4:1], ImmB[11], INSTRUCTION_t}), .sel(aa));
  Subtractor #(.width(32)) subtractor_1 (.a(shifter_1_out), .b(32'h1), .out(subtractor_1_out));  // open: bin, bout
  Comparator #(.width(7)) comparator_1 (.a(INSTRUCTION_t), .b(7'b0000011), .eq(I1));  // open: gt, lt
  Comparator #(.width(7)) comparator_2 (.a(INSTRUCTION_t), .b(7'b0010011), .eq(I2));  // open: gt, lt
  assign ImmI[31:11] = {{20{func7[6]}}, func7[6]};  // Bit_Extender bit_extender_1
  assign ImmS = {{20{func7[6]}}, func7[6]};  // Bit_Extender bit_extender_2
  assign ImmB[31:12] = {{19{func7[6]}}, func7[6]};  // Bit_Extender bit_extender_3
  assign ImmJ[31:20] = {{11{func7[6]}}, func7[6]};  // Bit_Extender bit_extender_4
  assign instr = I1 ? controlled_buffer_4_out : 5'bz;  // Controlled_Buffer controlled_buffer_1
  assign instr = I2 ? controlled_buffer_7_out : 5'bz;  // Controlled_Buffer controlled_buffer_2
  assign instr = S ? 5'b11000 : 5'bz;  // Controlled_Buffer controlled_buffer_3
  Multiplexer #(.select(3), .width(32), .enable("false")) multiplexer_2 (
    .in0({32{1'b0}}), .in1({ImmI[31:11], func7[5:0], ImmI[4:0]}), .in2({ImmI[31:11], func7[5:0], ImmI[4:0]}),
    .in3({ImmS, func7[5:0], ImmB[4:1], ImmB[11]}), .in4(subtractor_1_out),
    .in5({func7, ImmI[4:0], ImmJ[19:15], func3, {12{1'b0}}}),
    .in6({ImmJ, func3, ImmI[0], func7[5:0], ImmI[4:1], 1'b0}), .in7({ImmI[31:11], func7[5:0], ImmI[4:0]}),
    .out(Imm), .sel(ImmSel));
  Comparator #(.width(7)) comparator_3 (.a(INSTRUCTION_t), .b(7'b0100011), .eq(S));  // open: gt, lt
  assign controlled_buffer_4_out = comparator_4_eq ? 5'b01101 : 5'bz;  // Controlled_Buffer controlled_buffer_4
  Comparator #(.width(3)) comparator_4 (.a(func3), .b(3'b000), .eq(comparator_4_eq));  // open: gt, lt
  assign controlled_buffer_4_out = comparator_5_eq ? 5'b01110 : 5'bz;  // Controlled_Buffer controlled_buffer_5
  Comparator #(.width(3)) comparator_5 (.a(func3), .b(3'b001), .eq(comparator_5_eq));  // open: gt, lt
  assign controlled_buffer_4_out = comparator_6_eq ? 5'b01111 : 5'bz;  // Controlled_Buffer controlled_buffer_6
  Comparator #(.width(3)) comparator_6 (.a(func3), .b(3'b010), .eq(comparator_6_eq));  // open: gt, lt
  assign controlled_buffer_7_out = comparator_7_eq ? 5'b10000 : 5'bz;  // Controlled_Buffer controlled_buffer_7
  Comparator #(.width(3)) comparator_7 (.a(func3), .b(3'b000), .eq(comparator_7_eq));  // open: gt, lt
  assign controlled_buffer_7_out = comparator_8_eq ? 5'b10001 : 5'bz;  // Controlled_Buffer controlled_buffer_8
  Comparator #(.width(3)) comparator_8 (.a(func3), .b(3'b001), .eq(comparator_8_eq));  // open: gt, lt
  assign controlled_buffer_7_out = comparator_9_eq ? 5'b10010 : 5'bz;  // Controlled_Buffer controlled_buffer_9
  Comparator #(.width(3)) comparator_9 (.a(func3), .b(3'b010), .eq(comparator_9_eq));  // open: gt, lt
  assign controlled_buffer_7_out = comparator_10_eq ? 5'b10011 : 5'bz;  // Controlled_Buffer controlled_buffer_10
  Comparator #(.width(3)) comparator_10 (.a(func3), .b(3'b100), .eq(comparator_10_eq));  // open: gt, lt
  assign controlled_buffer_7_out = comparator_11_eq ? controlled_buffer_14_out : 5'bz;  // Controlled_Buffer controlled_buffer_11
  Comparator #(.width(3)) comparator_11 (.a(func3), .b(3'b101), .eq(comparator_11_eq));  // open: gt, lt
  assign controlled_buffer_7_out = comparator_12_eq ? 5'b10110 : 5'bz;  // Controlled_Buffer controlled_buffer_12
  Comparator #(.width(3)) comparator_12 (.a(func3), .b(3'b110), .eq(comparator_12_eq));  // open: gt, lt
  assign controlled_buffer_7_out = comparator_13_eq ? 5'b10111 : 5'bz;  // Controlled_Buffer controlled_buffer_13
  Comparator #(.width(3)) comparator_13 (.a(func3), .b(3'b111), .eq(comparator_13_eq));  // open: gt, lt
  BitFinder bitfinder_1 (.in({I3, J, U, SB, S, I2, I1, R}), .index(ImmSel));  // open: found
  assign controlled_buffer_14_out = comparator_14_eq ? 5'b10100 : 5'bz;  // Controlled_Buffer controlled_buffer_14
  Comparator #(.width(7)) comparator_14 (.a(func7), .b({7{1'b0}}), .eq(comparator_14_eq));  // open: gt, lt
  assign controlled_buffer_14_out = comparator_15_eq ? 5'b10101 : 5'bz;  // Controlled_Buffer controlled_buffer_15
  Comparator #(.width(7)) comparator_15 (.a(func7), .b(7'b0100000), .eq(comparator_15_eq));  // open: gt, lt
  Shifter #(.width(32)) shifter_2 (.in(WB), .\dist (5'b00010), .out(shifter_2_out));
  Comparator #(.width(32), .mode("unsigned")) comparator_16 (
    .a(Rrs1), .b(Rrs2), .eq(BrUn), .lt(UnsignedBrLT));  // open: gt
  Comparator #(.width(32)) comparator_17 (.a(Rrs1), .b(Rrs2), .eq(BrUn), .lt(SignedBrLT));  // open: gt
  Subtractor #(.width(32)) subtractor_2 (.a(shifter_2_out), .b(32'h4), .out(subtractor_2_out));  // open: bin, bout
  Multiplexer #(.select(3), .enable("false")) multiplexer_3 (
    .in0(1'b0), .in1(1'b0), .in2(1'b0), .in3(1'b0), .in4(1'b1), .in5(1'b0), .in6(1'b1), .in7(1'b0),
    .out(Asel), .sel(ImmSel));
  Multiplexer #(.select(3), .enable("false")) multiplexer_4 (
    .in0(1'b0), .in1(1'b1), .in2(1'b1), .in3(1'b1), .in4(1'b1), .in5(1'b1), .in6(1'b1), .in7(1'b1),
    .out(Bsel), .sel(ImmSel));
  Comparator #(.width(7)) comparator_18 (.a(INSTRUCTION_t), .b(7'b1100011), .eq(SB));  // open: gt, lt
  // mem_main DMEM: pin names not known; wires that end beside it: 32'hfff00513, result, Rrs2, MenRW, CLOCK, 32'h80006f, 32'h8067, ReadData, DMEM_p9, DMEM_p10
  Multiplexer #(.select(3), .width(32), .enable("false")) multiplexer_5 (
    .in0(WB), .in1(WB), .in2(WB), .in3(WB), .in4(WB), .in5(WB), .in6(subtractor_2_out),
    .in7(subtractor_2_out), .out(multiplexer_5_out), .sel(ImmSel));
  assign instr = SB ? controlled_buffer_20_out : 5'bz;  // Controlled_Buffer controlled_buffer_16
  Comparator #(.width(7)) comparator_19 (.a(INSTRUCTION_t), .b(7'b0110111), .eq(U));  // open: gt, lt
  Comparator #(.width(7)) comparator_20 (.a(INSTRUCTION_t), .b(7'b1101111), .eq(J));  // open: gt, lt
  Comparator #(.width(7)) comparator_21 (.a(INSTRUCTION_t), .b(7'b1100111), .eq(I3));  // open: gt, lt
  Multiplexer #(.width(32), .enable("false")) multiplexer_6 (.in0(Rrs2), .in1(Imm), .out(B), .sel(Bsel));
  assign instr = U ? 5'b11101 : 5'bz;  // Controlled_Buffer controlled_buffer_17
  assign instr = J ? 5'b11110 : 5'bz;  // Controlled_Buffer controlled_buffer_18
  assign instr = I3 ? {5{1'b1}} : 5'bz;  // Controlled_Buffer controlled_buffer_19
  Multiplexer #(.width(32), .enable("false")) multiplexer_7 (.in0(Rrs1), .in1(FETCH_ADDRESS), .out(A), .sel(Asel));
  assign controlled_buffer_20_out = comparator_22_eq ? 5'b11001 : 5'bz;  // Controlled_Buffer controlled_buffer_20
  Comparator #(.width(3)) comparator_22 (.a(func3), .b(3'b000), .eq(comparator_22_eq));  // open: gt, lt
  assign controlled_buffer_20_out = comparator_23_eq ? 5'b11010 : 5'bz;  // Controlled_Buffer controlled_buffer_21
  Comparator #(.width(3)) comparator_23 (.a(func3), .b(3'b100), .eq(comparator_23_eq));  // open: gt, lt
  assign controlled_buffer_20_out = comparator_24_eq ? 5'b11011 : 5'bz;  // Controlled_Buffer controlled_buffer_22
  Comparator #(.width(3)) comparator_24 (.a(func3), .b(3'b110), .eq(comparator_24_eq));  // open: gt, lt
  assign controlled_buffer_20_out = comparator_25_eq ? 5'b11100 : 5'bz;  // Controlled_Buffer controlled_buffer_23
  Comparator #(.width(3)) comparator_25 (.a(func3), .b(3'b001), .eq(comparator_25_eq));  // open: gt, lt
  Multiplexer #(.select(5), .width(4), .enable("false")) multiplexer_8 (
    .in0(4'b0000), .in1(4'b1010), .in2(4'b1100), .in3(4'b0110), .in4(4'b1110), .in5(4'b1011), .in6(4'b0111),
    .in7(4'b0011), .in8(4'b1000), .in9(4'b0100), .in10(4'b0010), .in11(4'b1001), .in12(4'b0001),
    .in13(4'b0000), .in14(4'b0000), .in15(4'b0000), .in16(4'b0000), .in17(4'b0110), .in18(4'b0111),
    .in19(4'b0011), .in20(4'b0100), .in21(4'b0101), .in22(4'b0010), .in23(4'b0001), .in24(4'b0000),
    .in25(4'b0000), .in26(4'b0000), .in27(4'b0000), .in28(4'b0000), .in29(4'b0000), .in30(4'b0000),
    .in31(4'b0000), .out(ALUsel), .sel(instr));
  Multiplexer #(.select(5), .enable("false")) multiplexer_9 (
    .in0(1'b1), .in1(1'b1), .in2(1'b1), .in3(1'b1), .in4(1'b1), .in5(1'b1), .in6(1'b1), .in7(1'b1),
    .in8(1'b1), .in9(1'b1), .in10(1'b1), .in11(1'b1), .in12(1'b1), .in13(1'b1), .in14(1'b1), .in15(1'b1),
    .in16(1'b1), .in17(1'b1), .in18(1'b1), .in19(1'b1), .in20(1'b1), .in21(1'b1), .in22(1'b1), .in23(1'b1),
    .in24(1'b0), .in25(1'b0), .in26(1'b0), .in27(1'b0), .in28(1'b0), .in29(1'b1), .in30(1'b1), .in31(1'b1),
    .out(regWen), .sel(instr));
  assign instr = R ? controlled_buffer_25_out : 5'bz;  // Controlled_Buffer controlled_buffer_24
  Comparator #(.width(7)) comparator_26 (.a(INSTRUCTION_t), .b(7'b0110011), .eq(R));  // open: gt, lt
  assign controlled_buffer_25_out = comparator_27_eq ? controlled_buffer_33_out : 5'bz;  // Controlled_Buffer controlled_buffer_25
  Comparator #(.width(3)) comparator_27 (.a(func3), .b(3'b000), .eq(comparator_27_eq));  // open: gt, lt
  assign controlled_buffer_25_out = comparator_28_eq ? controlled_buffer_36_out : 5'bz;  // Controlled_Buffer controlled_buffer_26
  Comparator #(.width(3)) comparator_28 (.a(func3), .b(3'b001), .eq(comparator_28_eq));  // open: gt, lt
  assign controlled_buffer_25_out = comparator_29_eq ? 5'b00101 : 5'bz;  // Controlled_Buffer controlled_buffer_27
  Comparator #(.width(3)) comparator_29 (.a(func3), .b(3'b011), .eq(comparator_29_eq));  // open: gt, lt
  assign controlled_buffer_25_out = comparator_30_eq ? 5'b00110 : 5'bz;  // Controlled_Buffer controlled_buffer_28
  Comparator #(.width(3)) comparator_30 (.a(func3), .b(3'b010), .eq(comparator_30_eq));  // open: gt, lt
  assign controlled_buffer_25_out = comparator_31_eq ? 5'b00111 : 5'bz;  // Controlled_Buffer controlled_buffer_29
  Comparator #(.width(3)) comparator_31 (.a(func3), .b(3'b100), .eq(comparator_31_eq));  // open: gt, lt
  assign controlled_buffer_25_out = comparator_32_eq ? controlled_buffer_38_out : 5'bz;  // Controlled_Buffer controlled_buffer_30
  Comparator #(.width(3)) comparator_32 (.a(func3), .b(3'b101), .eq(comparator_32_eq));  // open: gt, lt
  assign controlled_buffer_25_out = comparator_33_eq ? 5'b01010 : 5'bz;  // Controlled_Buffer controlled_buffer_31
  Comparator #(.width(3)) comparator_33 (.a(func3), .b(3'b110), .eq(comparator_33_eq));  // open: gt, lt
  assign controlled_buffer_25_out = comparator_34_eq ? controlled_buffer_40_out : 5'bz;  // Controlled_Buffer controlled_buffer_32
  Comparator #(.width(3)) comparator_34 (.a(func3), .b(3'b111), .eq(comparator_34_eq));  // open: gt, lt
  regfile_main RegFile (
    .rs2(ImmI[4:0]), .rd({ImmB[4:1], ImmB[11]}), .Read_Data_1(Rrs1), .Read_Data_2(Rrs2), .ra(ra), .sp(sp),
    .t0(t0), .t1(t1), .t2(t2), .s0(s0), .s1(s1), .a0(a0), .rs1(ImmJ[19:15]), .Write_Data(multiplexer_5_out),
    .RegWEn(regWen), .in_6(CLOCK));
  Multiplexer #(.select(5), .enable("false")) multiplexer_10 (
    .in0(1'b0), .in1(1'b0), .in2(1'b0), .in3(1'b0), .in4(1'b0), .in5(1'b0), .in6(1'b0), .in7(1'b0),
    .in8(1'b0), .in9(1'b0), .in10(1'b0), .in11(1'b0), .in12(1'b0), .in13(1'b0), .in14(1'b0), .in15(1'b0),
    .in16(1'b0), .in17(1'b0), .in18(1'b0), .in19(1'b0), .in20(1'b0), .in21(1'b0), .in22(1'b0), .in23(1'b0),
    .in24(1'b1), .in25(1'b0), .in26(1'b0), .in27(1'b0), .in28(1'b0), .in29(1'b0), .in30(1'b0), .in31(1'b0),
    .out(MenRW), .sel(instr));
  Multiplexer #(.select(5), .width(2), .enable("false")) multiplexer_11 (
    .in0(2'b01), .in1(2'b01), .in2(2'b01), .in3(2'b01), .in4(2'b01), .in5(2'b01), .in6(2'b01), .in7(2'b01),
    .in8(2'b01), .in9(2'b01), .in10(2'b01), .in11(2'b01), .in12(2'b01), .in13(2'b10), .in14(2'b10),
    .in15(2'b10), .in16(2'b01), .in17(2'b01), .in18(2'b01), .in19(2'b01), .in20(2'b01), .in21(2'b01),
    .in22(2'b01), .in23(2'b01), .in24(2'b11), .in25(2'b11), .in26(2'b11), .in27(2'b11), .in28(2'b11),
    .in29(2'b01), .in30(2'b00), .in31(2'b00), .out(WBSel), .sel(instr));
  assign controlled_buffer_33_out = comparator_35_eq ? {5{1'b0}} : 5'bz;  // Controlled_Buffer controlled_buffer_33
  Comparator #(.width(7)) comparator_35 (.a(func7), .b({7{1'b0}}), .eq(comparator_35_eq));  // open: gt, lt
  assign controlled_buffer_33_out = comparator_36_eq ? 5'b00001 : 5'bz;  // Controlled_Buffer controlled_buffer_34
  Comparator #(.width(7)) comparator_36 (.a(func7), .b(7'b0000001), .eq(comparator_36_eq));  // open: gt, lt
  assign controlled_buffer_33_out = comparator_37_eq ? 5'b00010 : 5'bz;  // Controlled_Buffer controlled_buffer_35
  Comparator #(.width(7)) comparator_37 (.a(func7), .b(7'b0100000), .eq(comparator_37_eq));  // open: gt, lt
  assign controlled_buffer_36_out = comparator_38_eq ? 5'b00011 : 5'bz;  // Controlled_Buffer controlled_buffer_36
  Comparator #(.width(7)) comparator_38 (.a(func7), .b({7{1'b0}}), .eq(comparator_38_eq));  // open: gt, lt
  assign controlled_buffer_36_out = comparator_39_eq ? 5'b00100 : 5'bz;  // Controlled_Buffer controlled_buffer_37
  Comparator #(.width(7)) comparator_39 (.a(func7), .b(7'b0000001), .eq(comparator_39_eq));  // open: gt, lt
  assign controlled_buffer_38_out = comparator_40_eq ? 5'b01000 : 5'bz;  // Controlled_Buffer controlled_buffer_38
  Comparator #(.width(7)) comparator_40 (.a(func7), .b(7'b0000001), .eq(comparator_40_eq));  // open: gt, lt
  assign controlled_buffer_38_out = comparator_41_eq ? 5'b01001 : 5'bz;  // Controlled_Buffer controlled_buffer_39
  Comparator #(.width(7)) comparator_41 (.a(func7), .b({7{1'b0}}), .eq(comparator_41_eq));  // open: gt, lt
  assign controlled_buffer_40_out = comparator_42_eq ? 5'b01011 : 5'bz;  // Controlled_Buffer controlled_buffer_40
  Comparator #(.width(7)) comparator_42 (.a(func7), .b(7'b0000001), .eq(comparator_42_eq));  // open: gt, lt
  assign controlled_buffer_40_out = comparator_43_eq ? 5'b01100 : 5'bz;  // Controlled_Buffer controlled_buffer_41
  Comparator #(.width(7)) comparator_43 (.a(func7), .b({7{1'b0}}), .eq(comparator_43_eq));  // open: gt, lt
  not not_1 (not_1_out, BrUn);
  Shifter #(.width(32), .shift("ar")) shifter_3 (.in(B), .\dist (5'b00010), .out(shifter_3_out));
  Multiplexer #(.select(2), .width(32), .enable("false")) multiplexer_12 (
    .in0(fetch_addr4), .in1(result), .in2(ReadData2), .out(WB), .sel(WBSel));  // open: in3
  Shifter #(.width(32), .shift("ar")) shifter_4 (.in(A), .\dist (5'b00010), .out(shifter_4_out));
  Shifter #(.width(32), .shift("ar")) shifter_5 (.in(B), .\dist (5'b00010), .out(shifter_5_out));
  Adder #(.width(32)) adder_1 (.a(FETCH_ADDRESS), .b(32'h1), .out(fetch_addr4));  // open: cin, cout
  Multiplexer #(.select(5), .enable("false")) multiplexer_13 (
    .in0(1'b0), .in1(1'b0), .in2(1'b0), .in3(1'b0), .in4(1'b0), .in5(1'b0), .in6(1'b0), .in7(1'b0),
    .in8(1'b0), .in9(1'b0), .in10(1'b0), .in11(1'b0), .in12(1'b0), .in13(1'b0), .in14(1'b0), .in15(1'b0),
    .in16(1'b0), .in17(1'b0), .in18(1'b0), .in19(1'b0), .in20(1'b0), .in21(1'b0), .in22(1'b0), .in23(1'b0),
    .in24(1'b0), .in25(BrUn), .in26(SignedBrLT), .in27(UnsignedBrLT), .in28(not_1_out), .in29(1'b0),
    .in30(1'b1), .in31(1'b1), .out(PCSel), .sel(instr));
  Multiplexer #(.select(3), .width(32), .enable("false")) multiplexer_14 (
    .in0(A), .in1(A), .in2(A), .in3(A), .in4(A), .in5(A), .in6(A), .in7(shifter_4_out),
    .out(multiplexer_14_out), .sel(ImmSel));
  Subtractor #(.width(32)) subtractor_3 (.a(shifter_3_out), .b(32'h1), .out(subtractor_3_out));  // open: bin, bout
  Register #(.width(32)) register_2 (.D(multiplexer_15_out), .clk(CLOCK), .Q(FETCH_ADDRESS));  // open: en, clr
  Multiplexer #(.width(32), .enable("false")) multiplexer_15 (
    .in0(fetch_addr4), .in1(result), .out(multiplexer_15_out), .sel(PCSel));
  Multiplexer #(.select(3), .width(32), .enable("false")) multiplexer_16 (
    .in0(B), .in1(B), .in2(B), .in3(B), .in4(B), .in5(B), .in6(subtractor_3_out), .in7(shifter_5_out),
    .out(multiplexer_16_out), .sel(ImmSel));
  Comparator #(.width(1)) comparator_44 (.a(1'b1), .b(PCSel), .eq(comparator_44_eq));  // open: gt, lt
  alu Arithmetic_Logic_Unit (.A(multiplexer_14_out), .B(multiplexer_16_out), .ALUSel(ALUsel), .Result(result));
  assign bit_extender_5_out = {{28{bit_extender_6_out[3]}}, bit_extender_6_out};  // Bit_Extender bit_extender_5
  Bit_Extender #(.in_width(32), .out_width(4)) bit_extender_6 (.in(ReadData), .out(bit_extender_6_out));
  Bit_Extender #(.in_width(32)) bit_extender_7 (.in(ReadData), .out(bit_extender_7_out));
  assign bit_extender_8_out = {{16{bit_extender_7_out[15]}}, bit_extender_7_out};  // Bit_Extender bit_extender_8
  Multiplexer #(.width(32), .enable("false")) multiplexer_17 (
    .in0({32{1'b0}}), .in1(32'h13), .out(multiplexer_17_out), .sel(comparator_44_eq));
  assign PCSel = comparator_45_eq ? 1'b0 : 1'bz;  // Controlled_Buffer controlled_buffer_42
  Comparator #(.width(32)) comparator_45 (
    .a({func7, ImmI[4:0], ImmJ[19:15], func3, ImmB[4:1], ImmB[11], INSTRUCTION_t}), .b({32{1'b0}}),
    .eq(comparator_45_eq));  // open: gt, lt
  Register #(.width(32)) register_3 (.D(multiplexer_17_out), .clk(CLOCK), .Q(ins));  // open: en, clr
  Multiplexer #(.select(5), .width(32), .enable("false")) multiplexer_18 (
    .in13(bit_extender_5_out), .in14(bit_extender_8_out), .in15(ReadData), .out(ReadData2), .sel(instr));  // open: in0, in1, in2, in3, in4, in5, in6, in7, in8, in9, in10, in11, in12, in16, in17, in18, in19, in20, in21, in22, in23, in24, in25, in26, in27, in28, in29, in30, in31
  Comparator #(.width(32)) comparator_46 (.a(ins), .b(32'h13), .eq(aa));  // open: gt, lt

  // Other names for the same wires on the sheet: clk = CLOCK; fetch_addr[31:0] = FETCH_ADDRESS;
  //   ImmS[10:0] = {func7[5:0], ImmB[4:1], ImmB[11]};
  //   INSTRUCTION_t[31:7] = {func7, ImmI[4:0], ImmJ[19:15], func3, ImmB[4:1], ImmB[11]};
  //   rd[4:0] = {ImmB[4:1], ImmB[11]}; ImmJ[14:1] = {func3, ImmI[0], func7[5:0], ImmI[4:1]};
  //   ImmU[31:12] = {func7, ImmI[4:0], ImmJ[19:15], func3}; rs2[4:0] = ImmI[4:0]; ImmB[10:5] = func7[5:0];
  //   ImmI[10:5] = func7[5:0]; rs1[4:0] = ImmJ[19:15]; inst[31:0] = INSTRUCTION; instr2[4:0] = instr;
  //   opcode[6:0] = INSTRUCTION_t

  // Notes on the sheet:
  //   Output
  //   Inputs/Outputs from run.circ. DO NOT MOVE THESE.
  //   Inputs
  //   Inputs/Outputs from run.circ. DO NOT MOVE THESE.
endmodule
